# Fritzing sketch breadbord   (saved by Fritzing 0.9.10b)
breadboards: 1

parts:
  U1 = STM32F303 [package=LQFP-48]
  TTL_/_USB = USB TTL Serial Cable
  TTL_/_RS485 = RS485 Module (MAX3485)
  TTL/RS485 = RS485 Module (MAX3485)
  pc_simulation_PLC_&_HMI = USB Connectors [package=usb-a-s]  # not connected
  LED1 = smd LED [color="Red (633nm)" package="1206 [SMD]"]
  LED = smd LED [color="Red (633nm)" package="1206 [SMD]"]
  LED3 = smd LED [color="Red (633nm)" package="1206 [SMD]"]
  220 = Resistor [tolerance=±5% package="2512 [SMD]"]
  Light_Sensor = BH1750

nets:
  N1: U1.A0, 220.Pin_0
  N2: U1.3V3#18, Light_Sensor.VCC
  N3: U1.GND#19, LED1.cathode, LED.cathode, LED3.cathode, Light_Sensor.GND
  N4: U1.A9, TTL/RS485.DE
  N5: U1.A10, TTL/RS485.DI
  N6: U1.B6, Light_Sensor.SCL
  N7: U1.B7, Light_Sensor.SDA
  N8: U1.5V#38, TTL/RS485.RO
  N9: U1.GNS, TTL/RS485.RE
  N10: TTL_/_USB.RX, TTL_/_RS485.RE
  N11: TTL_/_USB.TX, TTL_/_RS485.RO
  N12: TTL_/_USB.5V, TTL_/_RS485.DI
  N13: TTL_/_USB.GND, TTL_/_RS485.DE
  GND: TTL_/_RS485.GND, TTL/RS485.GND
  N14: TTL_/_RS485.A, TTL/RS485.B
  N15: TTL_/_RS485.B, TTL/RS485.A
  VCC: TTL_/_RS485.VCC, TTL/RS485.VCC
  N16: LED1.anode, LED.anode, LED3.anode, 220.Pin_1

custom parts:
  STM32F303: Medium density Cortex-M3 microcontroller.
  RS485 Module (MAX3485): Commercially available RS485 to RS232 TTL Module
  BH1750: Light Sensor
